// Logisim project adder.circ as structural Verilog: 1 circuit, main circuit main
module main (
);

  wire A, and_1_out, and_2_out, and_3_out, B, C, carry, clock_1_out, go, Reset_out, sum, t_ff_1_q, t_ff_2_q,
       t_ff_3_q;

  xor xor_1 (sum, A, B, C);
  and and_1 (and_1_out, A, B);
  and and_2 (and_2_out, A, C);
  and and_3 (and_3_out, B, C);
  or or_1 (carry, and_1_out, and_2_out, and_3_out);
  // Probe on {A, B, C}
  Clock clock_1 (.out(clock_1_out));
  T_Flip_Flop t_ff_1 (.clk(clock_1_out), .T(1'b1), .Q(t_ff_1_q), .Qn(C), .preset(Reset_out), .en(go));  // open: reset
  T_Flip_Flop t_ff_2 (.clk(t_ff_1_q), .T(1'b1), .Q(t_ff_2_q), .Qn(B), .preset(Reset_out));  // open: reset, en
  TTY #(.rows(1), .cols(8)) tty_1 (.data({5'b01100, carry, sum}), .clk(clock_1_out), .we(go), .clr(Reset_out));
  T_Flip_Flop t_ff_3 (.clk(t_ff_2_q), .T(1'b1), .Q(t_ff_3_q), .Qn(A), .preset(Reset_out));  // open: reset, en
  T_Flip_Flop t_ff_4 (.clk(t_ff_3_q), .T(1'b1), .Q(go), .preset(Reset_out));  // open: Qn, reset, en
  Button Reset (.out(Reset_out));

  // Notes on the sheet:
  //   multiple input = odd # input = 1
  //   01121223
endmodule
