// Logisim project alu.circ as structural Verilog
module main (
);

  wire A0, A1, A2, Ad0, Ad1, Ad2, Ad3, and_4_out, and_5_out, B0, B1, B2, C0, C1, C2, C_1, C_2, C_3,
       carryin_2_out, carryin_3_out, carryin_out, CIN, cinp0p1p2_out, clock_1_out, G0, g0p1p2_out, G1,
       g1p2_out, G2, not_1_out, not_2_out, not_3_out, not_4_out, P0, p0_c0_out, P1, p1_g0_out, P2, Reset_out,
       S0, S1, stop, xor_1_out, xor_2_out, xor_3_out;
  wire [11:3] rom_1_data;

  and and_1 (G0, A0, B0);
  or or_1 (P0, B0, A0);
  and and_2 (G1, A1, B1);
  or or_2 (P1, B1, A1);
  and and_3 (G2, A2, B2);
  or or_3 (P2, B2, A2);
  and p0_c0 (p0_c0_out, CIN, P0);
  or g0_plus (C_1, p0_c0_out, G0);
  and p1_g0 (p1_g0_out, G0, P1);
  and and_4 (and_4_out, CIN, P0, P1);
  and g1p2 (g1p2_out, G1, P2);
  and g0p1p2 (g0p1p2_out, G0, P1, P2);
  and cinp0p1p2 (cinp0p1p2_out, CIN, P0, P1);
  or g1_plus (C_2, p1_g0_out, and_4_out, G1);
  or plus_g2 (C_3, g1p2_out, g0p1p2_out, cinp0p1p2_out, G2);
  not not_1 (not_1_out, A0);
  xor xor_1 (xor_1_out, A0, B0);
  not not_2 (not_2_out, A1);
  xor xor_2 (xor_2_out, A1, B1);
  not not_3 (not_3_out, A2);
  xor xor_3 (xor_3_out, A2, B2);
  xor carryin (carryin_out, xor_1_out, CIN);
  xor carryin_2 (carryin_2_out, xor_2_out, C_1);
  xor carryin_3 (carryin_3_out, xor_3_out, C_2);
  Multiplexer #(.select(2)) multiplexer_1 (
    .in0(G0), .in1(P0), .in2(not_1_out), .in3(carryin_out), .out(C0), .sel({S1, S0}));  // open: en
  Multiplexer #(.select(2)) multiplexer_2 (
    .in0(G1), .in1(P1), .in2(not_2_out), .in3(carryin_2_out), .out(C1), .sel({S1, S0}));  // open: en
  Multiplexer #(.select(2)) multiplexer_3 (
    .in0(G2), .in1(P2), .in2(not_3_out), .in3(carryin_3_out), .out(C2), .sel({S1, S0}));  // open: en
  Clock clock_1 (.out(clock_1_out));
  // Probe on {C2, C1, C0}
  not not_4 (not_4_out, stop);
  // Probe on {S1, S0}
  // Probe on CIN
  TTY #(.rows(1), .cols(10)) tty_1 (.data({4'b0110, C2, C1, C0}), .clk(and_5_out), .clr(Reset_out));  // open: we
  and and_5 (and_5_out, clock_1_out, not_4_out);
  Counter #(.width(4), .max('ha), .ongoal("stay")) counter_1 (
    .Q({Ad3, Ad2, Ad1, Ad0}), .carry(stop), .clk(and_5_out), .clr(Reset_out));  // open: load, D, count
  ROM #(.addrWidth(4), .dataWidth(12)) rom_1 (
    .addr({Ad3, Ad2, Ad1, Ad0}),
    .data({rom_1_data[11], CIN, S1, S0, rom_1_data[7], B2, B1, B0, rom_1_data[3], A2, A1, A0}));  // open: sel
  // Probe on {B2, B1, B0}
  // Probe on {rom_1_data[11], CIN, S1, S0, rom_1_data[7], B2, B1, B0, rom_1_data[3], A2, A1, A0}
  // Probe on {A2, A1, A0}
  Button Reset (.out(Reset_out));

  // Notes on the sheet:
  //   Generating P/G
  //   Carry Look Ahead (generating carries)
  //   cin*p0*p1
  //   CHANGED HEREEEEE!!!!!!
  //   G = AND
  //   adder...
  //   adder...
  //   adder...
  //   NOT A
  //   P = OR
  //   adds 48 to make printable
  //   contents of rom_1 (hex, n*v repeats v):
  //   53 62 153 162 205 202 377 353 764 723
  //   5 & 3, 6 & 2, 5 | 3, 6 | 2, ~5, ~2, 7 + 7 + 0, 5 + 3 + 0, 6 + 4 + 1, 3 + 2 + 1
  //   1276256036
endmodule
