// Logisim project alutest.circ as structural Verilog
module main (
);

  wire A, A1, A2, Ad0, Ad1, Ad2, Ad3, and_2_out, B, B1, B2, C0, C1, C2, CIN, clock_1_out, not_1_out,
       Reset_out, S0, S1, stop;
  wire [11:3] rom_1_data;

  // AND_Gate AND has open pins: in0=A, in4=B, out=open
  Clock clock_1 (.out(clock_1_out));
  // Probe on {C2, C1, C0}
  not not_1 (not_1_out, stop);
  // Probe on {S1, S0}
  // Probe on CIN
  TTY #(.rows(1), .cols(10)) tty_1 (.data({4'b0110, C2, C1, C0}), .clk(and_2_out), .clr(Reset_out));  // open: we
  and and_2 (and_2_out, clock_1_out, not_1_out);
  Counter #(.width(4), .max('ha), .ongoal("stay")) counter_1 (
    .Q({Ad3, Ad2, Ad1, Ad0}), .carry(stop), .clk(and_2_out), .clr(Reset_out));  // open: load, D, count
  ROM #(.addrWidth(4), .dataWidth(12)) rom_1 (
    .addr({Ad3, Ad2, Ad1, Ad0}),
    .data({rom_1_data[11], CIN, S1, S0, rom_1_data[7], B2, B1, B, rom_1_data[3], A2, A1, A}));  // open: sel
  // Probe on {B2, B1, B}
  // Probe on {rom_1_data[11], CIN, S1, S0, rom_1_data[7], B2, B1, B, rom_1_data[3], A2, A1, A}
  // Probe on {A2, A1, A}
  Button Reset (.out(Reset_out));

  // Other names for the same wires on the sheet: B0 = B; A0 = A

  // Notes on the sheet:
  //   adds 48 to make printable
  //   contents of rom_1 (hex, n*v repeats v):
  //   53 62 153 162 205 202 377 353 764 723
  //   5 & 3, 6 & 2, 5 | 3, 6 | 2, ~5, ~2, 7 + 7 + 0, 5 + 3 + 0, 6 + 4 + 1, 3 + 2 + 1
  //   1276256036
endmodule
